# Fritzing sketch Moisture_LEDs (saved by Fritzing 0.9.4)
breadboards: 1

parts:
  Part4 = Arduino Uno (Rev3) - ICSP
  Part5 = LCD1602-I2C
  LED1 = LED - 3mm [color="Blue (505nm)" package="3 mm [THT]"]
  LED2 = LED - 3mm [color="Yellow (592nm)" package="3 mm [THT]"]
  LED3 = LED - 3mm [color="Green (560nm)" package="3 mm [THT]"]
  R1 = Resistor [tolerance=±5% resistance=220 package="1206 [SMD]"]
  R2 = Resistor [tolerance=±5% resistance=220 package="1206 [SMD]"]
  R3 = Resistor [tolerance=±5% resistance=220 package="1206 [SMD]"]
  BAT1 = Battery Holders [package=battery-aa]
  BUTTON1 = Arcade Button (red)
  Part9 = PowerBoost 1000 Basic  # not connected
  R4 = Resistor [tolerance=±5% resistance=10k package="1206 [SMD]"]

nets:
  N1: Part4.A4/SDA, Part5.SDA
  N2: Part4.A5/SCL, Part5.SCL
  N3: Part4.D2, R2.Pin_1
  N4: Part4.D3_PWM, R3.Pin_1
  N5: Part4.D4, R1.Pin_1
  5V: Part4.5V, Part5.VCC, LED1.anode, LED2.anode, LED3.anode
  GND: Part4.GND, Part5.GND, R4.Pin_0
  N6: LED1.cathode, R2.Pin_0
  N7: LED2.cathode, R1.Pin_0
  N8: LED3.cathode, R3.Pin_0
  N9: BAT1.+, BUTTON1.no_name_yet#1

notes:
  Nail #1
  Nail #2

custom parts:
  LCD1602-I2C: A standard character display, usually with 2x16 characters. Comes in many colors with LCM1602 IIC attached.
  Arcade Button (red): Adafruit Arcade Button (red)
  PowerBoost 1000 Basic: The PowerBoost 1000 is a little DC/DC boost converter module that can run from 1.8V batteries or higher, and convert the battery output to 5.2V DC for running your 5V projects. At its heart is a TPS61030 boost converter from TI. This boost converter chip has some really nice extras such as low battery detection, 4A internal switch, synchronous conversion, excellent efficiency, and 700KHz high-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
