# Fritzing sketch TempHum_ServoM (saved by Fritzing 0.9.4)
breadboards: 1

parts:
  Part1 = LCD1602-I2C
  Part2 = Arduino Uno (Rev3) - ICSP
  RHT1 = Humidity and Temperature Sensor RHT03
  R1 = Resistor [tolerance=±5% resistance=10k package=THT]
  Part10 = PowerBoost 1000 Basic
  BAT2 = Battery Holders [package=battery-aa]
  BUTTON2 = Arcade Button (red)
  J1 = Basic Servo

nets:
  GND: Part1.GND, Part2.GND, RHT1.GND_2, J1.gnd
  VCC: Part1.VCC, Part2.5V, RHT1.Vcc, R1.Pin_1, J1.vcc
  N1: Part1.SDA, Part2.A4/SDA
  N2: Part1.SCL, Part2.A5/SCL
  N3: Part2.D8, RHT1.Data-signal, R1.Pin_0
  N4: Part2.D5_PWM, J1.pulse
  N5: Part10.GND, Part10.ENABLE, Part10.LBO, Part10.5.0V
  N6: BAT2.+, BUTTON2.no_name_yet#1

custom parts:
  LCD1602-I2C: A standard character display, usually with 2x16 characters. Comes in many colors with LCM1602 IIC attached.
  PowerBoost 1000 Basic: The PowerBoost 1000 is a little DC/DC boost converter module that can run from 1.8V batteries or higher, and convert the battery output to 5.2V DC for running your 5V projects. At its heart is a TPS61030 boost converter from TI. This boost converter chip has some really nice extras such as low battery detection, 4A internal switch, synchronous conversion, excellent efficiency, and 700KHz high-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
  Arcade Button (red): Adafruit Arcade Button (red)
